# Fritzing sketch dpad-rear-terminal (saved by Fritzing 1.0.5)
circuit board: 4.33823cm x 4.06075cm
breadboards: 1

parts:
  B1 = Pushbutton [package=THT]
  B2 = Pushbutton [package=THT]
  B4 = Pushbutton [package=THT]
  B3 = Pushbutton [package=THT]
  R3 = Resistor [tolerance=±5% power=0.25W resistance=10k package=THT]
  R4 = Resistor [tolerance=±5% power=0.25W resistance=47k package=THT]
  R2 = Resistor [tolerance=±5% power=0.25W resistance=4.7k package=THT]
  R1 = Resistor [tolerance=±5% power=0.25W resistance=220 package=THT]
  RS = Resistor [tolerance=±5% power=0.25W resistance=10k package=THT]
  J1 = male pin header, 3 pins [form="♂ (male)"]

nets:
  N1: B1.leg0, B2.leg0, B4.leg0, B3.leg0, J1.pin1
  N2: B1.leg1, R1.Pin_0
  N3: B2.leg1, R2.Pin_0
  N4: B4.leg1, R4.Pin_0
  N5: B3.leg1, R3.Pin_0
  N6: R3.Pin_1, R4.Pin_1, R2.Pin_1, R1.Pin_1, RS.Pin_0, J1.pin3
  N7: RS.Pin_1, J1.pin2

notes:
  Parallel Resistor Ladder from
  https://github.com/bxparks/AceButton/blob/develop/docs/resistor_ladder/README.md
  GND
  VCC
  SEN
  dPAD
  2025 BPM
  Simple resistor ladder D-Pad
  tree/develop/docs/resistor_ladder
  Based on https://github.com/bxparks/AceButton/
  RS 10kΩ
  R3 10kΩ
  R1 220Ω
  R2 4.7kΩ
  R4 47kΩ
  Sample code: https://github.com/BrynM/dPAD
